// Logisim project RISC_V_CPU.circ as structural Verilog: 7 circuits, main circuit CPU
module CPU (
);

  wire [9:0] program_counter_1_out_5;

  Program_Counter program_counter_1 (.out_5(program_counter_1_out_5));  // open: in_2, in_3, in_4, in_1
  Instruction_Decoder instruction_decoder_1 ();  // open: in_1, in_2, in_3, in_4
  Instruction_Memory instruction_memory_1 (.in_1(program_counter_1_out_5));  // open: out_2
  Register_File register_file_1 ();  // open: read_reg_2, read_reg_1, write_data, reset, RegWrite, write_reg, read_data_1, read_data_2
  ALU alu_1 ();  // open: a, b_or_imm, result
endmodule

module Program_Counter (
  input  [9:0] in_1,
  input  in_2,
  input  in_3,
  input  in_4,
  output [9:0] out_5
);

  Counter #(.max('h3ff), .width(10)) counter_1 (
    .clr(in_2), .load(in_3), .clk(in_4), .D(in_1), .Q(out_5));  // open: up, count, carry

  // Other names for the same wires on the sheet: ADDR_IN[9:0] = in_1; ADDR_OUT[9:0] = out_5
endmodule

module Instruction_Memory (
  input  [9:0] in_1,
  output [31:0] out_2
);

  ROM #(.addrWidth(10), .dataWidth(32)) rom_1 (.addr(in_1), .data(out_2));

  // Other names for the same wires on the sheet: ADDR_IN[9:0] = in_1; ADDR_OUT[31:0] = out_2
endmodule

module Instruction_Decoder (
  input  [31:0] in_1,
  input  [6:0] in_2,
  input  in_3,
  input  in_4
);

  wire and_5_out, and_6_out, and_7_out, and_8_out, and_9_out, and_10_out, b_type, clk, i_type, imm_valid,
       j_type, or_3_out, or_4_out, r_type, rd_valid, rs1_valid, rs2_valid, s_type, u_type;
  wire [4:0] i_imm;
  wire [6:6] funct7;
  wire [9:7] dec_bits;
  wire [12:1] b_imm;
  wire [20:16] j_imm;

  Register #(.width(32)) Instruction_Register (
    .D(in_1), .clk(clk), .Q({funct7[6], b_imm[10:5], i_imm, j_imm, dec_bits, b_imm[4:1], b_imm[12], in_2}));  // open: en, clr
  Clock clock_1 (.out(clk));
  and and_1 (u_type, ~in_2[6], in_2[4], ~in_2[3], in_2[2]);  // AND_Gate
  and and_2 (b_type, in_2[6], in_2[5], ~in_2[4], ~in_2[3], ~in_2[2]);  // AND_Gate
  and and_3 (s_type, ~in_2[6], in_2[5], ~in_2[4], ~in_2[3]);  // AND_Gate
  and and_4 (j_type, in_2[6], in_2[5], ~in_2[4], in_2[3], in_2[2]);  // AND_Gate
  and and_5 (and_5_out, ~in_2[6], in_2[5]);  // AND_Gate
  and and_6 (and_6_out, in_2[6], ~in_2[5], in_2[4], ~in_2[3], ~in_2[2]);  // AND_Gate
  and and_7 (and_7_out, ~in_2[6], ~in_2[5], ~in_2[4], ~in_2[3]);  // AND_Gate
  and and_8 (and_8_out, ~in_2[6], ~in_2[5], in_2[4], ~in_2[2]);  // AND_Gate
  and and_9 (and_9_out, in_2[6], in_2[5], ~in_2[4], ~in_2[3], in_2[2]);  // AND_Gate
  and and_10 (and_10_out, ~in_2[6], ~b_imm[12], ~b_imm[1], ~b_imm[2], ~b_imm[3]);  // AND_Gate
  or or_1 (r_type, and_5_out, and_6_out);
  or or_2 (i_type, and_7_out, and_8_out, and_9_out);
  or or_3 (or_3_out, b_type, and_10_out, s_type);
  or or_4 (or_4_out, j_type, u_type);
  or or_5 (rs2_valid, r_type, s_type, b_type);
  not not_1 (rd_valid, or_3_out);
  not not_2 (imm_valid, r_type);
  not not_3 (rs1_valid, or_4_out);
  Comparator comparator_1 ();  // open: a, b, gt, eq, lt

  // Other names for the same wires on the sheet: ADDR_IN[31:0] = in_1; b_imm (some bits) = {b_imm[12], in_3};
  //   funct3[2:0] = dec_bits; j_imm[15:0] = {dec_bits, {2{i_imm[0]}}, b_imm[9:5], i_imm, in_4};
  //   u_imm[19:0] = {funct7[6], b_imm[10:5], i_imm, j_imm, dec_bits}; funct7[5:0] = b_imm[10:5];
  //   i_imm[11:5] = {funct7[6], b_imm[10:5]}; s_imm[11:0] = {funct7[6], b_imm[10:1], b_imm[12]};
  //   dec_bits (some bits) = {b_imm[10], in_2}; op[6:0] = in_2; rd[4:0] = {b_imm[4:1], b_imm[12]}; rs1[4:0] = j_imm;
  //   rs2[4:0] = i_imm

  // Notes on the sheet:
  //   Instruction Decoder
  //   Control Unit
  //   Validation of fields
  //   Instruction types
endmodule

module Arithmetic (
  input  [31:0] a,
  input  [31:0] b,
  output [31:0] y
);

  wire comparator_1_eq, comparator_1_gt, comparator_1_lt, not_1_out, or_1_out;

  Comparator #(.width(32)) comparator_1 (
    .a(a), .b(b), .gt(comparator_1_gt), .eq(comparator_1_eq), .lt(comparator_1_lt));
  Adder #(.width(32)) adder_1 (.a(a), .b(b), .out(y));  // open: cin, cout
  not not_1 (not_1_out, comparator_1_eq);
  or or_1 (or_1_out, comparator_1_gt, comparator_1_eq);
endmodule

module Register_File (
  input  [4:0] read_reg_2,
  input  [4:0] read_reg_1,
  input  [31:0] write_data,
  input  reset,
  input  RegWrite,
  input  [4:0] write_reg,
  output [31:0] read_data_1,
  output [31:0] read_data_2
);

  wire clock_tick_out, demultiplexer_1_out0, demultiplexer_1_out1, demultiplexer_1_out2,
       demultiplexer_1_out3, demultiplexer_1_out4, demultiplexer_1_out5, demultiplexer_1_out6,
       demultiplexer_1_out7, demultiplexer_1_out8, demultiplexer_1_out9, demultiplexer_1_out10,
       demultiplexer_1_out11, demultiplexer_1_out12, demultiplexer_1_out13, demultiplexer_1_out14,
       demultiplexer_1_out15, demultiplexer_1_out16, demultiplexer_1_out17, demultiplexer_1_out18,
       demultiplexer_1_out19, demultiplexer_1_out20, demultiplexer_1_out21, demultiplexer_1_out22,
       demultiplexer_1_out23, demultiplexer_1_out24, demultiplexer_1_out25, demultiplexer_1_out26,
       demultiplexer_1_out27, demultiplexer_1_out28, demultiplexer_1_out29, demultiplexer_1_out30,
       demultiplexer_1_out31;
  wire [31:0] register_1_q, register_2_q, register_3_q, register_4_q, register_5_q, register_6_q,
       register_7_q, register_8_q, register_9_q, register_10_q, register_11_q, register_12_q, register_13_q,
       register_14_q, register_15_q, register_16_q, register_17_q, register_18_q, register_19_q,
       register_20_q, register_21_q, register_22_q, register_23_q, register_24_q, register_25_q,
       register_26_q, register_27_q, register_28_q, register_29_q, register_30_q, register_31_q,
       register_32_q;

  Clock clock_tick (.out(clock_tick_out));
  Register #(.width(32)) register_1 (
    .D(write_data), .en(demultiplexer_1_out0), .clk(clock_tick_out), .Q(register_1_q), .clr(reset));
  Register #(.width(32)) register_2 (
    .D(write_data), .en(demultiplexer_1_out1), .clk(clock_tick_out), .Q(register_2_q), .clr(reset));
  Register #(.width(32)) register_3 (
    .D(write_data), .en(demultiplexer_1_out2), .clk(clock_tick_out), .Q(register_3_q), .clr(reset));
  Register #(.width(32)) register_4 (
    .D(write_data), .en(demultiplexer_1_out3), .clk(clock_tick_out), .Q(register_4_q), .clr(reset));
  Register #(.width(32)) register_5 (
    .D(write_data), .en(demultiplexer_1_out4), .clk(clock_tick_out), .Q(register_5_q), .clr(reset));
  Register #(.width(32)) register_6 (
    .D(write_data), .en(demultiplexer_1_out5), .clk(clock_tick_out), .Q(register_6_q), .clr(reset));
  Register #(.width(32)) register_7 (
    .D(write_data), .en(demultiplexer_1_out6), .clk(clock_tick_out), .Q(register_7_q), .clr(reset));
  Register #(.width(32)) register_8 (
    .D(write_data), .en(demultiplexer_1_out7), .clk(clock_tick_out), .Q(register_8_q), .clr(reset));
  Register #(.width(32)) register_9 (
    .D(write_data), .en(demultiplexer_1_out8), .clk(clock_tick_out), .Q(register_9_q), .clr(reset));
  Register #(.width(32)) register_10 (
    .D(write_data), .en(demultiplexer_1_out9), .clk(clock_tick_out), .Q(register_10_q), .clr(reset));
  Register #(.width(32)) register_11 (
    .D(write_data), .en(demultiplexer_1_out10), .clk(clock_tick_out), .Q(register_11_q), .clr(reset));
  Register #(.width(32)) register_12 (
    .D(write_data), .en(demultiplexer_1_out11), .clk(clock_tick_out), .Q(register_12_q), .clr(reset));
  Register #(.width(32)) register_13 (
    .D(write_data), .en(demultiplexer_1_out12), .clk(clock_tick_out), .Q(register_13_q), .clr(reset));
  Register #(.width(32)) register_14 (
    .D(write_data), .en(demultiplexer_1_out13), .clk(clock_tick_out), .Q(register_14_q), .clr(reset));
  Register #(.width(32)) register_15 (
    .D(write_data), .en(demultiplexer_1_out14), .clk(clock_tick_out), .Q(register_15_q), .clr(reset));
  Register #(.width(32)) register_16 (
    .D(write_data), .en(demultiplexer_1_out15), .clk(clock_tick_out), .Q(register_16_q), .clr(reset));
  Multiplexer #(.select(5), .width(32)) multiplexer_1 (
    .in0(register_1_q), .in1(register_2_q), .in2(register_3_q), .in3(register_4_q), .in4(register_5_q),
    .in5(register_6_q), .in6(register_7_q), .in7(register_8_q), .in8(register_9_q), .in9(register_10_q),
    .in10(register_11_q), .in11(register_12_q), .in12(register_13_q), .in13(register_14_q),
    .in14(register_15_q), .in15(register_16_q), .in16(register_17_q), .in17(register_18_q),
    .in18(register_19_q), .in19(register_20_q), .in20(register_21_q), .in21(register_22_q),
    .in22(register_23_q), .in23(register_24_q), .in24(register_25_q), .in25(register_26_q),
    .in26(register_27_q), .in27(register_28_q), .in28(register_29_q), .in29(register_30_q),
    .in30(register_31_q), .in31(register_32_q), .out(read_data_2), .sel(read_reg_2));
  Multiplexer #(.select(5), .width(32)) multiplexer_2 (
    .in0(register_1_q), .in1(register_2_q), .in2(register_3_q), .in3(register_4_q), .in4(register_5_q),
    .in5(register_6_q), .in6(register_7_q), .in7(register_8_q), .in8(register_9_q), .in9(register_10_q),
    .in10(register_11_q), .in11(register_12_q), .in12(register_13_q), .in13(register_14_q),
    .in14(register_15_q), .in15(register_16_q), .in16(register_17_q), .in17(register_18_q),
    .in18(register_19_q), .in19(register_20_q), .in20(register_21_q), .in21(register_22_q),
    .in22(register_23_q), .in23(register_24_q), .in24(register_25_q), .in25(register_26_q),
    .in26(register_27_q), .in27(register_28_q), .in28(register_29_q), .in29(register_30_q),
    .in30(register_31_q), .in31(register_32_q), .out(read_data_1), .sel(read_reg_1));
  Demultiplexer #(.select(5)) demultiplexer_1 (
    .out0(demultiplexer_1_out0), .out1(demultiplexer_1_out1), .out2(demultiplexer_1_out2),
    .out3(demultiplexer_1_out3), .out4(demultiplexer_1_out4), .out5(demultiplexer_1_out5),
    .out6(demultiplexer_1_out6), .out7(demultiplexer_1_out7), .out8(demultiplexer_1_out8),
    .out9(demultiplexer_1_out9), .out10(demultiplexer_1_out10), .out11(demultiplexer_1_out11),
    .out12(demultiplexer_1_out12), .out13(demultiplexer_1_out13), .out14(demultiplexer_1_out14),
    .out15(demultiplexer_1_out15), .out16(demultiplexer_1_out16), .out17(demultiplexer_1_out17),
    .out18(demultiplexer_1_out18), .out19(demultiplexer_1_out19), .out20(demultiplexer_1_out20),
    .out21(demultiplexer_1_out21), .out22(demultiplexer_1_out22), .out23(demultiplexer_1_out23),
    .out24(demultiplexer_1_out24), .out25(demultiplexer_1_out25), .out26(demultiplexer_1_out26),
    .out27(demultiplexer_1_out27), .out28(demultiplexer_1_out28), .out29(demultiplexer_1_out29),
    .out30(demultiplexer_1_out30), .out31(demultiplexer_1_out31), .in(RegWrite), .sel(write_reg));
  Register #(.width(32)) register_17 (
    .D(write_data), .en(demultiplexer_1_out16), .clk(clock_tick_out), .Q(register_17_q), .clr(reset));
  Register #(.width(32)) register_18 (
    .D(write_data), .en(demultiplexer_1_out17), .clk(clock_tick_out), .Q(register_18_q), .clr(reset));
  Register #(.width(32)) register_19 (
    .D(write_data), .en(demultiplexer_1_out18), .clk(clock_tick_out), .Q(register_19_q), .clr(reset));
  Register #(.width(32)) register_20 (
    .D(write_data), .en(demultiplexer_1_out19), .clk(clock_tick_out), .Q(register_20_q), .clr(reset));
  Register #(.width(32)) register_21 (
    .D(write_data), .en(demultiplexer_1_out20), .clk(clock_tick_out), .Q(register_21_q), .clr(reset));
  Register #(.width(32)) register_22 (
    .D(write_data), .en(demultiplexer_1_out21), .clk(clock_tick_out), .Q(register_22_q), .clr(reset));
  Register #(.width(32)) register_23 (
    .D(write_data), .en(demultiplexer_1_out22), .clk(clock_tick_out), .Q(register_23_q), .clr(reset));
  Register #(.width(32)) register_24 (
    .D(write_data), .en(demultiplexer_1_out23), .clk(clock_tick_out), .Q(register_24_q), .clr(reset));
  Register #(.width(32)) register_25 (
    .D(write_data), .en(demultiplexer_1_out24), .clk(clock_tick_out), .Q(register_25_q), .clr(reset));
  Register #(.width(32)) register_26 (
    .D(write_data), .en(demultiplexer_1_out25), .clk(clock_tick_out), .Q(register_26_q), .clr(reset));
  Register #(.width(32)) register_27 (
    .D(write_data), .en(demultiplexer_1_out26), .clk(clock_tick_out), .Q(register_27_q), .clr(reset));
  Register #(.width(32)) register_28 (
    .D(write_data), .en(demultiplexer_1_out27), .clk(clock_tick_out), .Q(register_28_q), .clr(reset));
  Register #(.width(32)) register_29 (
    .D(write_data), .en(demultiplexer_1_out28), .clk(clock_tick_out), .Q(register_29_q), .clr(reset));
  Register #(.width(32)) register_30 (
    .D(write_data), .en(demultiplexer_1_out29), .clk(clock_tick_out), .Q(register_30_q), .clr(reset));
  Register #(.width(32)) register_31 (
    .D(write_data), .en(demultiplexer_1_out30), .clk(clock_tick_out), .Q(register_31_q), .clr(reset));
  Register #(.width(32)) register_32 (
    .D(write_data), .en(demultiplexer_1_out31), .clk(clock_tick_out), .Q(register_32_q), .clr(reset));
endmodule

module ALU (
  input  [31:0] a,
  input  [31:0] b_or_imm,
  output [31:0] result
);

  Arithmetic arithmetic_1 (.a(a), .b(b_or_imm), .y(result));
endmodule
